# Fritzing sketch Colorsorter Microcontroller (saved by Fritzing 0.9.6b)
perfboards: 1

parts:
  Nano = Arduino Nano (Rev3.0)
  LightSensor = Adafruit APDS-9960 [part_number="Adafruit #3595"]
  Selector = Dagu DGServo 9g (End View) [part_number=RS001B]
  Ejector = Dagu DGServo 9g (End View) [part_number=RS001B]
  R1 = Resistor [tolerance=±5% power=0.25 resistance=100 package=THT]
  LED2 = LED - 3mm [color="Green (570nm)" package="3 mm [THT]"]
  LED1 = LED - 3mm [color="Red (633nm)" package="3 mm [THT]"]

nets:
  GND: Nano.GND, LightSensor.GND, Selector.gnd, Ejector.gnd, LED2.cathode, LED1.cathode
  N1: Nano.D5, Selector.pulse
  N2: Nano.D6, Ejector.pulse
  VCC: Nano.5V, Selector.vcc, Ejector.vcc, R1.Pin_0
  N3: Nano.A5, LightSensor.SCL
  N4: Nano.A4, LightSensor.SDA
  3V3: Nano.3V3, LightSensor.3.3V
  N5: R1.Pin_1, LED2.anode, LED1.anode

custom parts:
  Adafruit APDS-9960: The APDS9960 from Avago Technologies has an integrated IR LED and driver, along with four directional photodiodes that sense reflected IR energy from the LED. It's proximity detection feature allows it to measure the distance an object is from the front of the sensor (up to a few centimeters) with 8 bit resolution. Since there are four IR sensors, you can measure the changes in light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
